# Fritzing sketch resto2_0 (saved by Fritzing 0.9.3b)
breadboards: 1

parts:
  Part1 = Arduino Uno (Rev3)
  LCD1 = LCD screen
  R1 = Resistor [tolerance=±5% resistance=220 package=THT]
  R2 = Trimmer Potentiometer [maximum_resistance=10kΩ package=THT]
  J1 = Piezo Speaker
  S1 = Pushbutton [package="[SMD]"]
  LED1 = smd LED [color="Red (633nm)" package="1206 [SMD]"]
  R3 = Resistor [tolerance=±5% resistance=220 package="0805 [SMD]"]
  R4 = Resistor [tolerance=±5% resistance=220 package="2010 [SMD]"]
  Composant1 = sensor_biometrico

nets:
  N1: Part1.D8, S1.Pin_1, S1.Pin_2, R4.Pin_1
  N2: Part1.D9_PWM, LED1.cathode
  N3: Part1.D10_PWM/SS, J1.pin2
  N4: Part1.D11_PWM/MOSI, LCD1.E
  N5: Part1.D12/MISO, LCD1.RS
  GND: Part1.GND, LCD1.VSS, LCD1.R/W, LCD1.LED-, R2.leg1, J1.pin1, R3.Pin_0, R4.Pin_0, Composant1.GND
  N6: Part1.D2, LCD1.DB7
  N7: Part1.D3_PWM, LCD1.DB6
  N8: Part1.D4, LCD1.DB5
  N9: Part1.D5_PWM, LCD1.DB4
  N10: Part1.D6_PWM, Composant1.TX
  N11: Part1.D7, Composant1.RX
  5V: Part1.5V, LCD1.VDD, R1.Pin_0, R2.leg2, S1.Pin_3, S1.Pin_4
  N12: LCD1.V0, R2.wiper
  N13: LCD1.LED+, R1.Pin_1
  N14: LED1.anode, R3.Pin_1

custom parts:
  sensor_biometrico: Adafruit Optical Fingerprint Sensor

// code stored in the sketch: resto_2.0.ino
#include <LiquidCrystal.h>
LiquidCrystal lcd(12,11,5,4,3,2);
//importation du module pour le lcd
#include <Adafruit_Fingerprint.h>
//importation pour le module de détecteur d'obstacle
#if (defined(__AVR__) || defined(ESP8266)) && !defined(__AVR_ATmega2560__)
SoftwareSerial mySerial(6, 7);
#else
#define mySerial Serial1
#endif

Adafruit_Fingerprint finger = Adafruit_Fingerprint(&mySerial);
uint8_t id;
const int buttonPin = 8;
const int ledPin = 9;
const int buzzerPin = 10;
int etatButton = 0;

//--------------------------------------------------
void setup()
{
  pinMode(ledPin,OUTPUT);
  pinMode(buttonPin,INPUT);
  pinMode(buzzerPin, OUTPUT);
  lcd.begin(16,2);
  lcd.setCursor(0,0);
  lcd.print("Bienvenue");
  lcd.setCursor(0,1);
  lcd.print("cher client");
  Serial.begin(9600);
  while (!Serial);  // For Yun/Leo/Micro/Zero/...
  delay(100);
  Serial.println("\n\nAdafruit Fingerprint sensor enrollment");

  // set the data rate for the sensor serial port
  finger.begin(57600);

  if (finger.verifyPassword()) {
    Serial.println("Détecteur d'empreinte détecté");
  } else {
    Serial.println("Absence de détecteur d'empreinte :(");
    while (1) { delay(1); }
  }

  Serial.println(F("Reading sensor parameters"));
  finger.getParameters();
  Serial.print(F("Status: 0x")); Serial.println(finger.status_reg, HEX);
  Serial.print(F("Sys ID: 0x")); Serial.println(finger.system_id, HEX);
  Serial.print(F("Capacity: ")); Serial.println(finger.capacity);
  Serial.print(F("Security level: ")); Serial.println(finger.security_level);
  Serial.print(F("Device address: ")); Serial.println(finger.device_addr, HEX);
  Serial.print(F("Packet len: ")); Serial.println(finger.packet_len);
  Serial.print(F("Baud rate: ")); Serial.println(finger.baud_rate);

    finger.getTemplateCount();

  if (finger.templateCount == 0) {
    Serial.print("Le détecteur d'empreinte n'a enrigistré aucune empreinte. \n Veuillez insérer votre empreinte");
  }
  else {
    Serial.println("Recherche d'empreintes");
      Serial.print("Le détecteur d'empreintes a enrigistré "); Serial.print(finger.templateCount); Serial.println(" empreintes digitales");
  }
}

//----------------------------------------
void loop()                
{
  finger.getTemplateCount();
  etatButton = digitalRead(buttonPin);
  if(etatButton == LOW){
        Serial.println("Enrigistrez votre empreinte");
        if(finger.templateCount < 127){
          lcd.clear();
          lcd.setCursor(0,0);
          lcd.print("Veuillez vous");
          lcd.setCursor(0,1);
          lcd.print("enrigistrer");
            id = finger.templateCount+1;
            getFingerprintEnroll(); //permet d'enrigistrer une empreinte
            lcd.clear();
            lcd.setCursor(0,0);
            lcd.print("Bienvenue");
            lcd.setCursor(0,1);
            lcd.print("Cher client");
            digitalWrite(ledPin,HIGH);
            delay(1500);
            digitalWrite(ledPin,LOW);
          }else{
              Serial.println("La base de données est pleine. \n Veuillez nous excusez.");
            }
        }else{
      getFingerprintID(); //permet de vérifier une empreinte
      delay(1000); 
    }   
}
//----------------------------------------
uint8_t getFingerprintID() {
  uint8_t p = finger.getImage();
  switch (p) {
    case FINGERPRINT_OK:
      Serial.println("Image capturé");
      break;
    case FINGERPRINT_NOFINGER:
      Serial.println("Empreinte non détecté");
      return p;
    case FINGERPRINT_PACKETRECIEVEERR:
      Serial.println("Erreur de communication");
      return p;
    case FINGERPRINT_IMAGEFAIL:
      Serial.println("Erreur sur l'image");
      return p;
    default:
      Serial.println("Erreur inconnu");
      return p;
  }

  // Capture terminé

  p = finger.image2Tz();
  switch (p) {
    case FINGERPRINT_OK:
      Serial.println("Image convertie");
      break;
    case FINGERPRINT_IMAGEMESS:
      Serial.println("Image désordonné");
      return p;
    case FINGERPRINT_PACKETRECIEVEERR:
      Serial.println("Erreur de communication");
      return p;
    case FINGERPRINT_FEATUREFAIL:
      Serial.println("caractère d'empreinte non détecté");
      return p;
    case FINGERPRINT_INVALIDIMAGE:
      Serial.println("trait d'empreinte non détecté");
      return p;
    default:
      Serial.println("Erreur inconnu");
      return p;
  }

  // Convertion terminé
  p = finger.fingerSearch();
  if (p == FINGERPRINT_OK) {
    Serial.println("Empreinte présente dans la base");
    lcd.clear();
    lcd.setCursor(0,0);
    lcd.print("Empreinte");
    lcd.setCursor(0,1);
    lcd.print("identifie");
    digitalWrite(ledPin,HIGH);
    delay(1500);
    digitalWrite(ledPin,LOW);
    lcd.clear();
    lcd.setCursor(0,0);
    lcd.print("Bienvenue");
    lcd.setCursor(0,1);
    lcd.print("Cher client");
    digitalWrite(ledPin,HIGH);
    delay(1500);
    digitalWrite(ledPin,LOW);
  } else if (p == FINGERPRINT_PACKETRECIEVEERR) {
    Serial.println("Erreur de communication");
    return p;
  } else if (p == FINGERPRINT_NOTFOUND) {
    digitalWrite(buzzerPin,HIGH);
    delay(100);
    for(int i=0;i<=5;i++){
      digitalWrite(buzzerPin,LOW);
      delay(100);
      digitalWrite(buzzerPin,HIGH);
      delay(100);
    }
    lcd.clear();
    lcd.setCursor(0,0);
    lcd.print("Empreinte");
    lcd.setCursor(0,1);
    lcd.print("non identifie");
    Serial.println("Empreinte absente dans la base");
    delay(1500);
    lcd.clear();
    lcd.setCursor(0,0);
    lcd.print("Bienvenue");
    lcd.setCursor(0,1);
    lcd.print("Cher client");
    return p;
  } else {
    Serial.println("Erreur inconnu");
    return p;
  }

  // Correspondance
  Serial.print("Id trouvé #"); Serial.print(finger.fingerID);
  Serial.print(" Avec une assurance de "); Serial.println(finger.confidence);

  return finger.fingerID;
}
//----------------------------------------
uint8_t getFingerprintEnroll() {

  int p = -1;
  Serial.print("Attente pour la validation d'empreinte #"); Serial.println(id);
  while (p != FINGERPRINT_OK) {
    p = finger.getImage();
    switch (p) {
    case FINGERPRINT_OK:
      Serial.println("Image prise");
      break;
    case FINGERPRINT_NOFINGER:
      Serial.println(".");
      break;
    case FINGERPRINT_PACKETRECIEVEERR:
      Serial.println("Erreur de communication");
      break;
    case FINGERPRINT_IMAGEFAIL:
      Serial.println("Erreur sur image");
      break;
    default:
      Serial.println("Erreur inconnu");
      break;
    }
  }

  // OK success!

  p = finger.image2Tz(1);
  switch (p) {
    case FINGERPRINT_OK:
      Serial.println("Image convertie");
      break;
    case FINGERPRINT_IMAGEMESS:
      Serial.println("Image désordonné");
      return p;
    case FINGERPRINT_PACKETRECIEVEERR:
      Serial.println("Erreur de communication");
      return p;
    case FINGERPRINT_FEATUREFAIL:
      Serial.println("Caractère d'empreintes non trouvé");
      return p;
    case FINGERPRINT_INVALIDIMAGE:
      Serial.println("Caractère d'empreintes non trouvé");
      return p;
    default:
      Serial.println("Erreur inconnu");
      return p;
  }

  Serial.println("Suppression empreintes");
  delay(2000);
  p = 0;
  while (p != FINGERPRINT_NOFINGER) {
    p = finger.getImage();
  }
  Serial.print("ID "); Serial.println(id);
  p = -1;
  Serial.println("Replacez le doigt");
  while (p != FINGERPRINT_OK) {
    p = finger.getImage();
    switch (p) {
    case FINGERPRINT_OK:
      Serial.println("Prise images");
      break;
    case FINGERPRINT_NOFINGER:
      Serial.print(".");
      break;
    case FINGERPRINT_PACKETRECIEVEERR:
      Serial.println("Erreur de communication");
      break;
    case FINGERPRINT_IMAGEFAIL:
      Serial.println("Erreur sur image");
      break;
    default:
      Serial.println("Erreur inconnu");
      break;
    }
  }

  // OK success!

  p = finger.image2Tz(2);
  switch (p) {
    case FINGERPRINT_OK:
      Serial.println("Image convertie");
      break;
    case FINGERPRINT_IMAGEMESS:
      Serial.println("Image désordonné");
      return p;
    case FINGERPRINT_PACKETRECIEVEERR:
      Serial.println("Erreur de communication");
      return p;
    case FINGERPRINT_FEATUREFAIL:
      Serial.println("Caractère d'empreintes non trouvé");
      return p;
    case FINGERPRINT_INVALIDIMAGE:
      Serial.println("Caractère d'empreintes non trouvé");
      return p;
    default:
      Serial.println("Erreur inconnu");
      return p;
  }

  // OK converted!
  Serial.print("Création de modèle pour #");  Serial.println(id);

  p = finger.createModel();
  if (p == FINGERPRINT_OK) {
    Serial.println("Correspondance d'empreintes");
  } else if (p == FINGERPRINT_PACKETRECIEVEERR) {
    Serial.println("Erreur de communication");
    return p;
  } else if (p == FINGERPRINT_ENROLLMISMATCH) {
    Serial.println("Pas de correspondance d'empreintes");
    return p;
  } else {
    Serial.println("Erreur inconnu");
    return p;
  }

  Serial.print("ID "); Serial.println(id);
  p = finger.storeModel(id);
  if (p == FINGERPRINT_OK) {
    Serial.println("Enrigistré");
    lcd.clear();
    lcd.setCursor(0,0);
    lcd.print("Empreinte");
    lcd.setCursor(0,1);
    lcd.print("enrigistre");
    digitalWrite(ledPin,HIGH);
    delay(500);
    digitalWrite(ledPin,LOW);
    delay(500);
    digitalWrite(ledPin,HIGH);
    delay(500);
    digitalWrite(ledPin,LOW);
    delay(2000);
    lcd.clear();
    lcd.setCursor(0,0);
    lcd.print("Bonjour");
    lcd.setCursor(0,1);
    lcd.print("Cher client");
  } else if (p == FINGERPRINT_PACKETRECIEVEERR) {
    Serial.println("Erreur de communication");
    return p;
  } else if (p == FINGERPRINT_BADLOCATION) {
    Serial.println("Defaut de stockage");
    return p;
  } else if (p == FINGERPRINT_FLASHERR) {
    Serial.println("Erreur d'écriture flash");
    return p;
  } else {
    Serial.println("Erreur inconnu");
    return p;
  }

  return true;
}
// ************ Par Michel Nassalang **************
